# Fritzing sketch wiring (saved by Fritzing 0.9.3b)
circuit board: 8.31076cm x 4.74602cm
breadboards: 1

parts:
  Bauteil1 = Arduino Nano (Rev3.0)
  VCC1 = Battery block 9V
  S1 = Toggle Switch [package=THT]
  U1 = JOYSTICK-PSP1000 [package=joystick-psp1000]
  S2 = Pushbutton [package="[THT]"]
  S3 = Pushbutton [package="[THT]"]
  R2 = Resistor [tolerance=±5% resistance=10k package=THT]
  J1 = single row smd male pin header, 3 pins [form="♂ (male)"]
  J2 = single row smd male pin header, 1 pin [form="♂ (male)"]
  J3 = single row smd male pin header, 1 pin [form="♂ (male)"]
  R3 = Resistor [tolerance=±5% resistance=220 package=THT]
  R4 = Resistor [tolerance=±5% resistance=470 package=THT]
  R1 = Resistor [tolerance=±5% resistance=10k package=THT]

nets:
  GND: Bauteil1.GND, S1.L2, U1.GND, R2.Pin_0, R1.Pin_0
  N1: Bauteil1.D3, J2.pin1
  N2: Bauteil1.D6, R3.Pin_1
  N3: Bauteil1.D7, R4.Pin_1
  N4: Bauteil1.D9, J3.pin1
  N5: Bauteil1.D11/MOSI, S2.Pin_3, S2.Pin_4, R1.Pin_1
  N6: Bauteil1.D12/MISO, S3.Pin_3, S3.Pin_4, R2.Pin_1
  N7: Bauteil1.VIN, VCC1.+
  5V: Bauteil1.5V, U1.VCC, S2.Pin_1, S2.Pin_2, S3.Pin_1, S3.Pin_2
  N8: Bauteil1.A2, U1.X
  N9: Bauteil1.A1, U1.Y
  N10: VCC1.-, S1.COM
  N11: J1.pin1, J1.pin2, R3.Pin_0
  N12: J1.pin3, R4.Pin_0

notes:
  optional power (on/off) switch
  RGB
  H-Sync
  V-Sync
